# Fritzing sketch TaskScheduler (saved by Fritzing 0.9.3b)
breadboards: 1

parts:
  LED1 = LED - 5mm [color="Red (633nm)" package="5 mm [THT]"]
  LED2 = LED - 5mm [color="Blue (525nm)" package="5 mm [THT]"]
  LED3 = LED - 5mm [color="Green (555nm)" package="5 mm [THT]"]
  R3 = Resistor [tolerance=±5% resistance=330 package=THT]
  Arduino1 = Arduino Uno (Rev3)
  R2 = Resistor [tolerance=±5% resistance=330 package=THT]
  R1 = Resistor [tolerance=±5% resistance=330 package=THT]
  R4 = Resistor [tolerance=±5% resistance=10k package=THT]
  R9 = Photocell (LDR) [package=THT]

nets:
  N1: LED1.cathode, R2.Pin_0
  N2: LED1.anode, Arduino1.D4
  N3: LED2.cathode, R1.Pin_0
  N4: LED2.anode, Arduino1.D3_PWM
  N5: LED3.cathode, R3.Pin_0
  N6: LED3.anode, Arduino1.D5_PWM
  N7: R3.Pin_1, Arduino1.GND, R2.Pin_1, R1.Pin_1, R4.Pin_1
  N8: Arduino1.A0, R4.Pin_0, R9.pin_1
  N9: Arduino1.5V, R9.pin_0

notes:
  FADER
  BLINKER (PIN13)
  OK
  ALARM
  PIN 3 ~
  PIN 4
  PIN 5
  A0
  PHOTOCELL
