# Fritzing sketch TaskScheduler_with_Sleep_BreadBoard_Pinout (saved by Fritzing 0.9.3b)
breadboards: 1

parts:
  LED1 = LED - 5mm [color="Red (633nm)" package="5 mm [THT]"]
  LED2 = LED - 5mm [color="Blue (525nm)" package="5 mm [THT]"]
  Arduino1 = Arduino Uno (Rev3)
  R2 = Resistor [tolerance=±5% resistance=330 package=THT]
  R1 = Resistor [tolerance=±5% resistance=330 package=THT]
  S1 = Pushbutton [package="[THT]"]

nets:
  N1: LED1.cathode, R2.Pin_0
  N2: LED1.anode, Arduino1.D6_PWM
  N3: LED2.cathode, R1.Pin_0
  N4: LED2.anode, Arduino1.D5_PWM
  N5: Arduino1.D2, S1.Pin_3, S1.Pin_4
  N6: Arduino1.GND, R2.Pin_1, R1.Pin_1, S1.Pin_1, S1.Pin_2

notes:
  FADER
  BLINKER
  PIN 6
  PIN 5
  PIN 2 (PULLUP)
  PCINT2_vect
